# Fritzing sketch Projeto X-All (saved by Fritzing 0.9.3b)
breadboards: 2

parts:
  Part1 = Arduino Uno (Rev3)
  Part2 = Arduino Nano (Rev3.0)
  Part3 = Arduino Mega 2560 (Rev3)
  hc-sr1 = hc-sr04
  hc-sr2 = hc-sr04
  Part4 = DeuLigne 1.1 - The Snootlab's LCD shield for Arduino  # not connected

nets:
  N1: Part1.A4/SDA, Part2.A4, Part3.D20/SDA
  N2: Part1.A5/SCL, Part2.A5, Part3.D21/SCL
  GND: Part1.GND, Part3.GND, hc-sr1.GND, hc-sr2.GND
  N3: Part2.D4, hc-sr2.Trig
  N4: Part2.D5, hc-sr2.Echo
  N5: Part2.D6, hc-sr1.Trig
  N6: Part2.D7, hc-sr1.Echo
  VCC: hc-sr1.VCC, hc-sr2.VCC
